// Logisim project y86.circ as structural Verilog
module main (
  input  Reset
);

  wire and_1_out, Clock_out, nor_1_out, not_1_out;
  wire [1:0] imem_1_p13, Stat_q;
  wire [3:0] icode, ifun, rA, rB;
  wire [7:0] imem_1_p4, imem_1_p5, imem_1_p6, imem_1_p7, imem_1_p8, imem_1_p9, imem_1_p10, imem_1_p11,
       imem_1_p12;
  wire [31:0] new_PC, pc_increment_1_val_p, PC_q, valA_0, valA_1, valB_0, valB_1, valc_0, valc_1, valE_0,
       valE_1, valM_0, valM_1;

  and and_1 (and_1_out, Clock_out, nor_1_out);
  Clock Clock (.out(Clock_out));
  Register #(.width(32)) PC (.D(new_PC), .Q(PC_q), .clk(and_1_out), .clr(Reset));  // open: en
  nor nor_1 (nor_1_out, Stat_q[1], Stat_q[0]);
  not not_1 (not_1_out, and_1_out);
  Register #(.width(2)) Stat (.D(imem_1_p13), .Q(Stat_q), .clk(not_1_out));  // open: en, clr
  // imem imem_1: pin names not known; wires that end beside it: new_PC, PC_q, {icode, ifun}, imem_1_p4, imem_1_p5, imem_1_p6, imem_1_p7, imem_1_p8, imem_1_p9, imem_1_p10, imem_1_p11, imem_1_p12, imem_1_p13
  Align align_1 (
    .B1(imem_1_p4), .B2(imem_1_p5), .B3(imem_1_p6), .B4(imem_1_p7), .B5(imem_1_p8), .B6(imem_1_p9),
    .B7(imem_1_p10), .B8(imem_1_p11), .B9(imem_1_p12), .rB(rB), .rA(rA), .valC_1(valc_1), .valC_0(valc_0));  // open: NeedRegs
  // regfile regfile_1: pin names not known; wires that end beside it: 4'b1111, rB, rB, valE_1, valE_0, 4'b1111, {32{1'b1}}, {32{1'b1}}, not_1_out, Reset, valA_1, valA_0, valB_1, valB_0
  alu ALU (
    .aluA_1(valc_1), .aluA_0(valc_0), .aluB_1({32{1'b0}}), .aluB_0({32{1'b0}}), .ALUfun(ifun),
    .valE_1(valE_1), .valE_0(valE_0));  // open: out_6, out_7, out_8
  // dmem dmem_1: pin names not known; wires that end beside it: valE_1, valE_0, {32{1'b0}}, {32{1'b0}}, 1'b0, 1'b0, not_1_out, Reset, valM_1, valM_0
  PC_Increment pc_increment_1 (.icode(icode), .ifun(ifun), .PC(PC_q), .Val_P(pc_increment_1_val_p));
  Register #(.width(32)) PChold (.D(pc_increment_1_val_p), .Q(new_PC), .clk(not_1_out), .clr(Reset));  // open: en

  // Notes on the sheet:
  //   Memory
  //   change destM
  //   reg inputs temporary
  //   a lot of this can be changed around later, just finna get irmovq working
  //   PC Inc
endmodule

module Align (
  input  [7:0] B1,
  input  [7:0] B2,
  input  [7:0] B3,
  input  [7:0] B4,
  input  [7:0] B5,
  input  [7:0] B6,
  input  [7:0] B7,
  input  [7:0] B8,
  input  [7:0] B9,
  input  NeedRegs,
  output [3:0] rB,
  output [3:0] rA,
  output [31:0] valC_1,
  output [31:0] valC_0
);

  wire [3:0] icode;

  Multiplexer #(.select(4)) multiplexer_1 (
    .in0(1'b0), .in1(1'b0), .in2(1'b1), .in3(1'b1), .in4(1'b1), .in5(1'b1), .in6(1'b1), .in7(1'b0),
    .in8(1'b0), .in9(1'b0), .in10(1'b1), .in11(1'b1), .in12(1'b1), .in13(1'b1), .in14(1'b1), .in15(1'b1),
    .out(NeedRegs), .sel(icode));  // open: en

  assign rA = B1[7:4];
  assign rB = B1[3:0];
  assign valC_0 = {B5, B4, B3, B2};
  assign valC_1 = {B6, B7, B8, B9};

  // Notes on the sheet:
  //   valC_0 is lower 32 bits, while valC_1 is upper 32, more significant, bits
endmodule

module PC_Increment (
  input  [3:0] icode,
  input  [3:0] ifun,
  input  [31:0] PC,
  output [31:0] Val_P
);

  wire [1:0] multiplexer_1_out, multiplexer_2_out;
  wire [31:0] multiplexer_3_out;

  Multiplexer #(.select(4), .width(2), .enable("false")) multiplexer_1 (
    .in0(2'b00), .in1(2'b00), .in2(2'b01), .in3(2'b11), .in4(2'b11), .in5(2'b11), .in6(2'b01), .in7(2'b10),
    .in8(2'b01), .in9(2'b10), .in10(2'b00), .in11(2'b01), .in12(2'b01), .out(multiplexer_1_out), .sel(icode));  // open: in13, in14, in15
  Multiplexer #(.select(2), .width(2), .enable("false")) multiplexer_2 (
    .in0(2'b00), .in1(2'b01), .in2(2'b10), .in3(2'b11), .out(multiplexer_2_out), .sel(multiplexer_1_out));
  Multiplexer #(.select(2), .width(32), .enable("false")) multiplexer_3 (
    .in0(32'h2), .in1(32'h4), .in2(32'h9), .in3(32'ha), .out(multiplexer_3_out), .sel(multiplexer_2_out));
  Adder #(.width(32)) adder_1 (.a(multiplexer_3_out), .b(PC), .out(Val_P));  // open: cin, cout

  // Notes on the sheet:
  //   PC Increment
  //   Input: icode, ifun, PC
  //   Output: The next value for PC, or Val P
  //   select 0, 1, 2, or 3 to pick a length
  //   choose between the 4 different lengths of the instruction to add
  //   Add PC to the length of the current instruction
  //   PC + Instruction Length
endmodule
